# Fritzing sketch schema (saved by Fritzing 0.9.3b)
circuit board: 5cm x 7cm

parts:
  Part3 = Arduino Nano (Rev3.0)
  Part4 = BH1750
  electronicsguy2 = electronicsguy 0.96" 128x64 SPI I2C OLED
  Minus = Pushbutton [package="[THT]"]
  Plus = Pushbutton [package="[THT]"]
  Priority = Pushbutton [package="[THT]"]
  Menu = Pushbutton [package="[THT]"]
  Metering = Pushbutton [package="[THT]"]
  Metering_Mode = Pushbutton [package="[THT]"]
  VCC2 = Battery
  Adafruit_P/N_1400 = Adafruit Push-button Power Switch Breakout [package=THT]

nets:
  GND: Part3.GND, Part4.GND, electronicsguy2.GND, Minus.Pin_3, Minus.Pin_4, Plus.Pin_3, Priority.Pin_3, Priority.Pin_4, Menu.Pin_3, Menu.Pin_4, Metering.Pin_3, Metering_Mode.Pin_3, Metering_Mode.Pin_4, VCC2.-, Adafruit_P/N_1400.GND
  N1: Part3.D2, Metering.Pin_1, Metering.Pin_2
  N2: Part3.D3, Plus.Pin_1
  N3: Part3.D4, Minus.Pin_1, Minus.Pin_2
  N4: Part3.D5, Priority.Pin_1
  N5: Part3.D6, Menu.Pin_1, Menu.Pin_2
  N6: Part3.D7, Metering_Mode.Pin_1, Metering_Mode.Pin_2
  N7: Part3.D8, electronicsguy2.D0
  N8: Part3.D9, electronicsguy2.D1
  N9: Part3.D10, electronicsguy2.RST
  N10: Part3.D11/MOSI, electronicsguy2.DC
  N11: Part3.D12/MISO, electronicsguy2.CS
  5V: Part3.5V, electronicsguy2.VCC, Adafruit_P/N_1400.OUT
  N12: Part3.A5, Part4.SCL
  N13: Part3.A4, Part4.SDA
  3V3: Part3.3V3, Part4.VCC
  N14: VCC2.+, Adafruit_P/N_1400.IN

custom parts:
  BH1750: Light Sensor
  electronicsguy 0.96" 128x64 SPI I2C OLED: Generic 0.96" 128x64 SPI I2C OLED Default is SPI mode Can be re-configured for I2C (needs soldering work) Comes in various colors like blue, white, yellow-blue
